# Fritzing sketch circuit (saved by Fritzing 0.9.3b)
breadboards: 1

parts:
  R1 = Resistor [tolerance=±5% resistance=220 package=THT]
  R2 = Resistor [tolerance=±5% resistance=330 package=THT]
  R3 = Resistor [tolerance=±5% resistance=1.2M package=THT]
  Infrared_LED = LTE-302 [package=lte-302]
  Phototransistor = LTR-301 [package=ltr-301]
  Componente1 = Arduino Nano (Rev3.0)

nets:
  N1: R1.Pin_0, R3.Pin_0, Componente1.5V
  N2: R1.Pin_1, R2.Pin_0, Infrared_LED.A
  N3: R2.Pin_1, Infrared_LED.C, Phototransistor.C, Componente1.GND
  N4: R3.Pin_1, Phototransistor.E, Componente1.A0
